# Fritzing sketch SketchOfEverthing (saved by Fritzing 0.9.3b)
breadboards: 1

parts:
  LED1 = LED - 5mm [color="Red (633nm)" package="5 mm [THT]"]
  LED2 = LED - 5mm [color="Yellow (595nm)" package="5 mm [THT]"]
  LED3 = LED - 5mm [color="Green (555nm)" package="5 mm [THT]"]
  R1 = Resistor [tolerance=±5% resistance=220 package=THT]
  S1 = Pushbutton [package="[THT]"]
  R2 = Resistor [tolerance=±5% resistance=220 package=THT]
  U2 = ESP32S-HiLetgo [part_number=ESP32S-HiLetgo]
  U3 = 4-Channel 5v Relay Shield [package=relay-4ch5v10a]
  WATER_PUMP1 = water pump/motor
  WATER_PUMP2 = water pump/motor
  U4 = DC-DC_CONVERTER [package=dc-dc_converter]

nets:
  N1: LED1.cathode, LED2.cathode, LED3.cathode, R1.Pin_0
  N2: LED1.anode, U2.GPIO19
  N3: LED2.anode, U2.GPIO18
  N4: LED3.anode, U2.GPIO5
  GND: R1.Pin_1, R2.Pin_0, U2.GND, U3.GND
  N5: S1.Pin_1, S1.Pin_2, R2.Pin_1, U2.GPIO17
  N6: S1.Pin_3, S1.Pin_4, U2.3.3
  N7: U2.GPIO33, U3.IN1
  N8: U2.GPIO25, U3.IN2
  VIN: U2.VIN, U3.VCC
  N9: U3.K1-Off, U3.K2-Off, U4.VOUT
  N10: U3.K1-On, WATER_PUMP2.pin_2
  N11: U3.K2-On, WATER_PUMP1.pin_2
  N12: WATER_PUMP1.pin_1, U4.GND2
  N13: WATER_PUMP2.pin_1, U4.GND1

custom parts:
  ESP32S-HiLetgo: HiLetgo ESP-WROOM-32 ESP32 ESP-32S Development Board 2.4GHz Dual-Mode WiFi + Bluetooth Dual Cores Microcontroller The ESP32 integrated with Antenna switches, RF Balun, power amplifiers, low-noise amplifiers, filters, and management modules, and the entire solution occupies the least area of PCB. 2.4 GHz Wi-Fi plus Bluetooth dual-mode chip, with TSMC Ultra-low power consumption 40nm technology,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
  4-Channel 5v Relay Shield: 4 Channel 5v Relay Shield w. 2x SPD-06VDC-SD-C
  water pump/motor: WATER PUMP BY ARDUBLOCKTR
